# Fritzing sketch esp8266_blynk_temp_sensor (saved by Fritzing 0.9.3b)
breadboards: 1

parts:
  Part1 = Arduino Nano (Rev3.0)
  T1 = TMP36 Temperature Sensor [package="TO92 [THT]"]
  U1 = ESP8266 WiFi Module [part_number=ESP8266]

nets:
  N1: Part1.D1/TX, U1.RXD
  N2: Part1.D0/RX, U1.TXD
  GND: Part1.GND, T1.GND, U1.GND
  N3: Part1.A0, T1.Vout
  3V3: Part1.AREF, Part1.3V3, T1.+Vs, U1.VCC, U1.CH_PD

custom parts:
  ESP8266 WiFi Module: Generic WiFi Module based on the ESP8266 with onboard PCB antenna and UART communications
